# Fritzing sketch EJ00.1_Led_resistor (saved by Fritzing 0.9.9b)
breadboards: 1

parts:
  LED1 = LED - 5mm [color="Red (633nm)" current=0.030 package="5 mm [THT]"]
  R1 = Resistor [tolerance=±5% power=0.25 resistance=220 package=THT]
  USBTTL1 = USB TTL Serial Cable

nets:
  N1: LED1.cathode, R1.Pin_1
  N2: LED1.anode, R1.Pin_0, USBTTL1.GND

notes:
  LED y resistor
  Copyright (C) 2024 Jesus D. Garza Camarena
  jesus.garzacmn@uanl.edu.mx
  Este documento es Open Hardware
  Licencia: CERN-OHL-S
  https://cern-ohl.web.cern.ch/home
