# Fritzing sketch EjS02.1ConTransistores (saved by Fritzing 0.9.9b)
breadboards: 1

parts:
  R1 = Resistor [tolerance=±5% resistance=330 power=0.25 package=THT]
  SW1 = DIP Switch 8 Position [package=dipswitch-08]
  LED2 = LED - 5mm [color="Red (633nm)" current=0.030 package="5 mm [THT]"]
  R2 = Resistor [tolerance=±5% resistance=330 power=0.25 package=THT]
  S1 = Pushbutton [package="[THT]"]
  LED3 = LED - 5mm [color="Yellow (595nm)" current=0.030 package="5 mm [THT]"]
  R3 = Resistor [tolerance=±5% resistance=330 power=0.25 package=THT]
  LED4 = LED - 5mm [color="Green (560nm)" current=0.030 package="5 mm [THT]"]
  S2 = Pushbutton [package="[THT]"]
  S3 = Pushbutton [package="[THT]"]
  R4 = Resistor [tolerance=±5% resistance=330 power=0.25 package=THT]
  LED5 = LED - 5mm [color="Blue (505nm)" current=0.030 package="5 mm [THT]"]
  S4 = Pushbutton [package="[THT]"]
  S5 = Pushbutton [package="[THT]"]
  R5 = Resistor [tolerance=±5% resistance=330 power=0.25 package=THT]
  P1 = Multimeter straight black probe
  P2 = Multimeter straight red probe
  S6 = Pushbutton [package="[THT]"]
  LED6 = LED - 5mm [color="Yellow (595nm)" current=0.030 package="5 mm [THT]"]
  USBTTL1 = USB TTL Serial Cable
  VM1 = Multimeter (DC Voltage)

nets:
  N1: R1.Pin_0, R3.Pin_0, R4.Pin_0, R5.Pin_0, S6.Pin_1, S6.Pin_2, LED6.cathode, USBTTL1.GND
  N2: R1.Pin_1, S1.Pin_1, S1.Pin_2
  N3: SW1.1, R3.Pin_1
  N4: SW1.16, LED2.cathode
  N5: R2.Pin_0, S6.Pin_3, S6.Pin_4, LED6.anode
  N6: R2.Pin_1, LED3.anode, LED4.anode, LED5.anode, USBTTL1.5V
  N7: S1.Pin_3, S1.Pin_4, LED3.cathode
  N8: LED4.cathode, S2.Pin_3, S2.Pin_4
  N9: S2.Pin_1, S2.Pin_2, S3.Pin_3, S3.Pin_4
  N10: S3.Pin_1, S3.Pin_2, R4.Pin_1
  N11: LED5.cathode, S4.Pin_3, S4.Pin_4, S5.Pin_3, S5.Pin_4
  N12: S4.Pin_1, S4.Pin_2, S5.Pin_1, S5.Pin_2, R5.Pin_1
  N13: P1.Probe_tip, P1.Probe_meter_end, VM1.COM_Probe
  N14: P2.Probe_meter_end, VM1.V_Probe

notes:
  Valores Lógicos Con Interruptores
  Copyright (C) 2024 Jesus D. Garza Camarena
  jesus.garzacmn@uanl.edu.mx
  Este documento es Open Hardware
  Licencia: CERN-OHL-S
  https://cern-ohl.web.cern.ch/home
  Conexion a una fuente de +5V
  Cable Rojo = + 5Vcd = Positivo
  Cable Negro = - GND = Negativo
