# Fritzing sketch EjS02.3CompuertasLógicas (saved by Fritzing 0.9.9b)
breadboards: 1

parts:
  S1 = Pushbutton [package="[THT]"]
  IC1 = IC, DIP package, 14 pins [chip_label=74LS04]
  IC2 = IC, DIP package, 14 pins [chip_label=74LS08]
  IC4 = IC, DIP package, 14 pins [chip_label=74LS32]
  IC5 = IC, DIP package, 14 pins [chip_label=74LS02]
  IC6 = IC, DIP package, 14 pins [chip_label=74HC86]
  S2 = Pushbutton [package="[THT]"]
  R3 = Resistor [tolerance=±5% resistance=330 power=0.25 package=THT]
  LED3 = LED - 5mm [color="Orange (620nm)" current=0.030 package="5 mm [THT]"]
  R1 = Resistor [tolerance=±5% resistance=330 power=0.25 package=THT]
  R2 = Resistor [tolerance=±5% resistance=330 power=0.25 package=THT]
  LED2 = LED - 5mm [color="Red (633nm)" current=0.030 package="5 mm [THT]"]
  LED3_2 = LED - 5mm [color="Red (633nm)" current=0.030 package="5 mm [THT]"]
  LED4 = LED - 5mm [color="Yellow (595nm)" current=0.030 package="5 mm [THT]"]
  R4 = Resistor [tolerance=±5% resistance=330 power=0.25 package=THT]
  R5 = Resistor [tolerance=±5% resistance=330 power=0.25 package=THT]
  LED5 = LED - 5mm [color="Green (570nm)" current=0.030 package="5 mm [THT]"]
  R6 = Resistor [tolerance=±5% resistance=330 power=0.25 package=THT]
  LED6 = LED - 5mm [color="Blue (525nm)" current=0.030 package="5 mm [THT]"]
  R7 = Resistor [tolerance=±5% resistance=330 power=0.25 package=THT]
  LED7 = LED - 5mm [color="White (4500K)" current=0.030 package="5 mm [THT]"]
  R8 = Resistor [tolerance=±5% resistance=330 power=0.25 package=THT]
  LED8 = LED - 5mm [color="Red (635nm)" current=0.030 package="5 mm [THT]"]
  IC3 = IC, DIP package, 14 pins [chip_label=74LS00]
  USBTTL1 = USB TTL Serial Cable

nets:
  N1: S1.Pin_1, S1.Pin_2, LED2.cathode
  N2: S1.Pin_3, S1.Pin_4, IC1.pin1, IC2.pin1, IC4.pin1, IC5.pin1, IC6.pin1, R1.Pin_0, IC3.pin1
  N3: IC1.pin2, LED3.anode
  N4: IC1.pin7, IC2.pin7, IC4.pin7, IC5.pin7, IC6.pin7, R3.Pin_0, R1.Pin_1, R2.Pin_1, R4.Pin_0, R5.Pin_0, R6.Pin_0, R7.Pin_0, R8.Pin_0, USBTTL1.GND
  N5: IC1.pin14, IC2.pin14, IC4.pin14, IC5.pin14, IC6.pin14, LED2.anode, LED3_2.anode, USBTTL1.5V
  N6: IC2.pin2, IC5.pin2, IC6.pin2, S2.Pin_3, S2.Pin_4, R2.Pin_0, IC3.pin2
  N7: IC2.pin3, LED4.anode
  N8: IC4.pin3, LED6.anode
  N9: IC5.pin3, LED7.anode
  N10: IC6.pin3, LED8.anode
  N11: S2.Pin_1, S2.Pin_2, LED3_2.cathode
  N12: R3.Pin_1, LED3.cathode
  N13: LED4.cathode, R4.Pin_1
  N14: R5.Pin_1, LED5.cathode
  N15: LED5.anode, IC3.pin3
  N16: R6.Pin_1, LED6.cathode
  N17: R7.Pin_1, LED7.cathode
  N18: R8.Pin_1, LED8.cathode

notes:
  Compuertas Lógicas TTL
  Copyright (C) 2024 Jesus D. Garza Camarena
  jesus.garzacmn@uanl.edu.mx
  Este documento es Open Hardware
  Licencia: CERN-OHL-S
  https://cern-ohl.web.cern.ch/home
