# Fritzing sketch EjS03.1_CapturaEsquemática (saved by Fritzing 0.9.9b)
breadboards: 1

parts:
  S1 = Pushbutton [package="[THT]"]
  S2 = Pushbutton [package="[THT]"]
  S4 = Pushbutton [package="[THT]"]
  R1 = Resistor [tolerance=±5% resistance=330 package="0603 [SMD]"]
  LED4 = LED - 5mm [color="Green (565nm)" current=0.030 package="5 mm [THT]"]
  LED5 = LED - 5mm [color="Yellow (595nm)" current=0.030 package="5 mm [THT]"]
  LED6 = LED - 5mm [color="Red (635nm)" current=0.030 package="5 mm [THT]"]
  R2 = Resistor [tolerance=±5% resistance=330 package="0603 [SMD]"]
  R3 = Resistor [tolerance=±5% resistance=330 package="0603 [SMD]"]
  R4 = Resistor [tolerance=±5% resistance=330 package="0603 [SMD]"]
  USBTTL2 = USB TTL Serial Cable
  U1 = IC, SIP package, 12 pins [chip_label="                   22V10"]
  LED10 = LED - 5mm [color="White (4500K)" current=0.030 package="5 mm [THT]"]
  LED11 = LED - 5mm [color="Orange (612nm)" current=0.030 package="5 mm [THT]"]
  LED12 = LED - 5mm [color="Red (635nm)" current=0.030 package="5 mm [THT]"]
  LED13 = LED - 5mm [color="Blue (525nm)" current=0.030 package="5 mm [THT]"]
  R5 = Resistor [tolerance=±5% resistance=330 package="0603 [SMD]"]
  R6 = Resistor [tolerance=±5% resistance=330 package="0603 [SMD]"]
  R7 = Resistor [tolerance=±5% resistance=330 package="0603 [SMD]"]
  R8 = Resistor [tolerance=±5% resistance=330 package="0603 [SMD]"]
  LED15 = LED - 5mm [color="Green (570nm)" current=0.030 package="5 mm [THT]"]

nets:
  N1: S1.Pin_1, S1.Pin_2, R3.Pin_1, U1.pin2
  N2: S1.Pin_3, S1.Pin_4, LED5.cathode
  N3: S2.Pin_1, S2.Pin_2, R4.Pin_1, U1.pin1
  N4: S2.Pin_3, S2.Pin_4, LED6.cathode
  N5: S4.Pin_1, S4.Pin_2, R2.Pin_1, U1.pin3
  N6: S4.Pin_3, S4.Pin_4, LED4.cathode
  N7: R1.Pin_0, R2.Pin_0, R3.Pin_0, R4.Pin_0, USBTTL2.GND, U1.pin12, R5.Pin_0, R6.Pin_0, R7.Pin_0, R8.Pin_0
  N8: R1.Pin_1, LED10.cathode
  N9: LED4.anode, LED5.anode, LED6.anode, USBTTL2.5V
  N10: LED11.cathode, R6.Pin_1
  N11: LED12.cathode, R5.Pin_1
  N12: LED13.cathode, R7.Pin_1
  N13: R8.Pin_1, LED15.cathode

notes:
  1
  2
  3
  4
  12
  24
  23
  Captura Esquemática
  Copyright (C) 2024 Jesus D. Garza Camarena
  jesus.garzacmn@uanl.edu.mx
  Este documento es Open Hardware
  Licencia: CERN-OHL-S
  https://cern-ohl.web.cern.ch/home

custom parts:
  Pushbutton: A generic pushbutton.
