# Fritzing sketch EjS04.1 (saved by Fritzing 0.9.9b)
breadboards: 1

parts:
  S1 = Pushbutton [package="[THT]"]
  S2 = Pushbutton [package="[THT]"]
  S4 = Pushbutton [package="[THT]"]
  R1 = Resistor [tolerance=±5% resistance=330 package="0603 [SMD]"]
  LED4 = LED - 5mm [color="Green (565nm)" current=0.030 package="5 mm [THT]"]
  LED5 = LED - 5mm [color="Yellow (595nm)" current=0.030 package="5 mm [THT]"]
  LED6 = LED - 5mm [color="Red (635nm)" current=0.030 package="5 mm [THT]"]
  R3 = Resistor [tolerance=±5% resistance=330 package="0603 [SMD]"]
  USBTTL2 = USB TTL Serial Cable
  U1 = IC, SIP package, 12 pins [chip_label="                   22V10"]
  LED10 = LED - 5mm [color="Blue (470nm)" current=0.030 package="5 mm [THT]"]
  R8 = Resistor [tolerance=±5% resistance=330 package="0603 [SMD]"]
  LED15 = LED - 5mm [color="White (4500K)" current=0.030 package="5 mm [THT]"]
  R9 = Resistor [tolerance=±5% resistance=330 package="0603 [SMD]"]
  S5 = Pushbutton [package="[THT]"]
  R10 = Resistor [tolerance=±5% resistance=330 package="0603 [SMD]"]
  LED16 = LED - 5mm [color="Red (635nm)" current=0.030 package="5 mm [THT]"]
  R11 = Resistor [tolerance=±5% resistance=330 package="0603 [SMD]"]

nets:
  N1: S1.Pin_1, S1.Pin_2, R3.Pin_1, U1.pin2
  N2: S1.Pin_3, S1.Pin_4, LED5.cathode
  N3: S2.Pin_1, S2.Pin_2, U1.pin1, R9.Pin_1
  N4: S2.Pin_3, S2.Pin_4, LED6.cathode
  N5: S4.Pin_1, S4.Pin_2, U1.pin3, R10.Pin_1
  N6: S4.Pin_3, S4.Pin_4, LED4.cathode
  N7: R1.Pin_0, R3.Pin_0, USBTTL2.GND, U1.pin12, R8.Pin_0, R9.Pin_0, R10.Pin_0, R11.Pin_0
  N8: R1.Pin_1, LED10.cathode
  N9: LED4.anode, LED5.anode, LED6.anode, USBTTL2.5V, LED16.anode
  N10: U1.pin4, S5.Pin_1, S5.Pin_2, R11.Pin_1
  N11: R8.Pin_1, LED15.cathode
  N12: S5.Pin_3, S5.Pin_4, LED16.cathode

notes:
  1
  2
  3
  4
  12
  24
  23
  Combinacional
  Copyright (C) 2024 Jesus D. Garza Camarena
  jesus.garzacmn@uanl.edu.mx
  Este documento es Open Hardware
  Licencia: CERN-OHL-S
  https://cern-ohl.web.cern.ch/home
  D
  C
  B
  A
  F1
  F2

custom parts:
  Pushbutton: A generic pushbutton.
