# Fritzing sketch P3 (saved by Fritzing 0.9.3b)
breadboards: 1

parts:
  S1 = Pushbutton [package="[THT]"]
  S2 = Pushbutton [package="[THT]"]
  S3 = Pushbutton [package="[THT]"]
  S4 = Pushbutton [package="[THT]"]
  R1 = Resistor [tolerance=±5% resistance=330 package="0603 [SMD]"]
  LED4 = LED - 5mm [color="Red (633nm)" package="5 mm [THT]"]
  LED5 = LED - 5mm [color="Yellow (595nm)" package="5 mm [THT]"]
  LED6 = LED - 5mm [color="Green (570nm)" package="5 mm [THT]"]
  LED9 = LED - 5mm [color="Red (635nm)" package="5 mm [THT]"]
  R2 = Resistor [tolerance=±5% resistance=330 package="0603 [SMD]"]
  R3 = Resistor [tolerance=±5% resistance=330 package="0603 [SMD]"]
  R4 = Resistor [tolerance=±5% resistance=330 package="0603 [SMD]"]
  R5 = Resistor [tolerance=±5% resistance=330 package="0603 [SMD]"]
  USBTTL2 = USB TTL Serial Cable
  U1 = IC, SIP package, 12 pins [chip_label="                   22V10"]
  LED10 = LED - 5mm [color="White (4500K)" package="5 mm [THT]"]

nets:
  N1: S1.Pin_1, S1.Pin_2, R3.Pin_1, U1.pin3
  N2: S1.Pin_3, S1.Pin_4, LED5.cathode
  N3: S2.Pin_1, S2.Pin_2, R4.Pin_1, U1.pin2
  N4: S2.Pin_3, S2.Pin_4, LED6.cathode
  N5: S3.Pin_1, S3.Pin_2, R5.Pin_1, U1.pin1
  N6: S3.Pin_3, S3.Pin_4, LED9.cathode
  N7: S4.Pin_1, S4.Pin_2, R2.Pin_1, U1.pin4
  N8: S4.Pin_3, S4.Pin_4, LED4.cathode
  N9: R1.Pin_0, R2.Pin_0, R3.Pin_0, R4.Pin_0, R5.Pin_0, USBTTL2.GND, U1.pin12
  N10: R1.Pin_1, LED10.cathode
  N11: LED4.anode, LED5.anode, LED6.anode, LED9.anode, USBTTL2.5V

notes:
  Actividad 4 Ejemplo
  1
  2
  3
  4
  12
  24
  23
  PLD (pin)
  ATF22v10C
  GAL22V10D
  VCC (24) / +5V
  GND (12)
  Clase Sistemas Digitales/ Electrónica Digital

custom parts:
  Pushbutton: A generic pushbutton.
