# Fritzing sketch EJ00.1_Led_resistor (saved by Fritzing 0.9.9b)
breadboards: 3

parts:
  USBTTL1 = USB TTL Serial Cable  # not connected
  P1 = Multimeter straight red probe  # not connected
  P2 = Multimeter straight black probe  # not connected
  VM1 = Multimeter (DC Voltage)  # not connected
  R7 = Resistor [tolerance=±5% resistance=220 power=0.25 package=THT]  # not connected
  D2 = Rectifier Diode [part_number=1N4001 package="300 mil [THT]"]  # not connected
  Q2 = PNP-Transistor [package="TO92 [THT]"]
  L2 = Inductor [package="400 mil [THT]"]
  IC2 = IC, DIP package, 8 pins [chip_label=IC]
  R8 = Resistor [tolerance=±5% resistance=220 power=0.25 package=THT]  # not connected
  D3 = Rectifier Diode [part_number=1N4001 package="300 mil [THT]"]  # not connected
  Q3 = PNP-Transistor [package="TO92 [THT]"]  # not connected
  L3 = Inductor [package="400 mil [THT]"]  # not connected
  IC3 = IC, DIP package, 8 pins [chip_label=IC]

nets:
  N1: Q2.C, L2.pin_1
  N2: L2.pin_0, IC2.pin5
  N3: IC3.pin1, IC3.pin3

notes:
  Ejemplo N°00 - Fuente de Voltaje
  JDGC
  Copyright (C) 2024 Jesus D. Garza Camarena
  jesus.garzacmn@uanl.edu.mx
  Este documento es Open Hardware
  Licencia: CERN-OHL-S
  https://cern-ohl.web.cern.ch/home
  Fila 1  (+)
  Fila 2 (-)
  Columnas
  Filas
  Ejemplo N°00 - Uso de protoboard
