# Fritzing sketch Ejemplo Protoboard (saved by Fritzing 0.9.3b)
breadboards: 3

parts:
  S1 = Pushbutton [package="[THT]"]
  LED1 = LED - 5mm [color="Red (633nm)" package="5 mm [THT]"]
  LED3 = LED - 5mm [color="Yellow (592nm)" package="5 mm [THT]"]
  LED4 = LED - 5mm [color="Green (565nm)" package="5 mm [THT]"]
  SW1 = DIP Switch 8 Position [package=dipswitch-08]
  R1 = Resistor [tolerance=±5% resistance=330 package=THT]
  R2 = Resistor [tolerance=±5% resistance=330 package=THT]
  S2 = Pushbutton [package="[THT]"]
  R3 = Resistor [tolerance=±5% resistance=330 package=THT]
  S3 = Pushbutton [package="[THT]"]
  S4 = Pushbutton [package="[THT]"]
  R5 = Resistor [tolerance=±5% resistance=330 package=THT]
  S5 = Pushbutton [package="[THT]"]
  LED5 = LED - 5mm [color="Red (633nm)" package="5 mm [THT]"]
  V1 = DC Power [voltage=5]  # not connected
  USBTTL1 = USB TTL Serial Cable
  R6 = Resistor [tolerance=±5% resistance=220 package=THT]  # not connected
  D1 = Rectifier Diode [part_number=1N4001 package="300 mil [THT]"]  # not connected
  Q1 = PNP-Transistor [package="TO92 [THT]"]
  L1 = Inductor [package="400 mil [THT]"]
  IC1 = IC, DIP package, 8 pins [chip_label=IC]

nets:
  N1: S1.Pin_1, S1.Pin_2, R2.Pin_1
  N2: S1.Pin_3, S1.Pin_4, LED3.cathode
  N3: LED1.cathode, SW1.16
  N4: LED1.anode, LED3.anode, LED4.anode, USBTTL1.5V
  N5: LED4.cathode, S2.Pin_3, S2.Pin_4
  N6: SW1.1, R1.Pin_1
  N7: R1.Pin_0, R2.Pin_0, R3.Pin_0, R5.Pin_0, USBTTL1.GND
  N8: S2.Pin_1, S2.Pin_2, S3.Pin_3, S3.Pin_4
  N9: R3.Pin_1, S3.Pin_1, S3.Pin_2
  N10: S4.Pin_1, S4.Pin_2, R5.Pin_1, S5.Pin_1, S5.Pin_2
  N11: S4.Pin_3, S4.Pin_4, S5.Pin_3, S5.Pin_4, LED5.cathode
  N12: Q1.C, L1.pin_1
  N13: L1.pin_0, IC1.pin5

notes:
  Conexion a una fuente de +5V
  Cable Rojo = + 5Vcd = Positivo
  Cable Negro = - GND = Negativo
  Práctica de laboratorio N°1
  Filas
  Columnas
  Fila 2 (-)
  Fila 1  (+)
